# Fritzing sketch New2 ping-pongv1 (saved by Fritzing 0.9.0b)
breadboards: 1

parts:
  Raspberry_Pi1 = Raspberry Pi B+
  R4 = Resistor [tolerance=±5% resistance=1k package=THT]
  R7 = Resistor [tolerance=±5% resistance=1k package=THT]
  R9 = Resistor [tolerance=±5% resistance=1k package=THT]
  R10 = Resistor [tolerance=±5% resistance=1k package=THT]
  R12 = Resistor [tolerance=±5% resistance=1k package=THT]
  R15 = Resistor [tolerance=±5% resistance=1k package=THT]
  R19 = Resistor [tolerance=±5% resistance=1k package=THT]
  R26 = Resistor [tolerance=±5% resistance=1k package=THT]
  S1 = Pushbutton [package="[THT]"]
  S2 = Pushbutton [package="[THT]"]
  LED2 = LED - 5mm [color="Red (633nm)" package="5 mm [THT]"]
  LED3 = LED - 5mm [color="Red (633nm)" package="5 mm [THT]"]
  LED4 = LED - 5mm [color="Red (633nm)" package="5 mm [THT]"]
  LED5 = LED - 5mm [color="Red (633nm)" package="5 mm [THT]"]
  LED6 = LED - 5mm [color="Red (633nm)" package="5 mm [THT]"]
  LED7 = LED - 5mm [color="Red (633nm)" package="5 mm [THT]"]
  R28 = Resistor [tolerance=±5% resistance=1k package=THT]
  U3 = 7-SEGMENT-DISPLAY-1_-RED [package=7-segment-1_pth]
  U4 = 7-SEGMENT-DISPLAY-1_-RED [package=7-segment-1_pth]
  R29 = Resistor [tolerance=±5% resistance=220 package=THT]
  U5 = Mystery Part - 2 pins [chip_label=Buzzer package=THT]

nets:
  3V3: Raspberry_Pi1.3v3, Raspberry_Pi1.3V3, Raspberry_Pi1.GIPO24, R4.Pin_0, R12.Pin_1, R26.Pin_0, S1.Pin_1, S1.Pin_2, S1.Pin_3, S1.Pin_4, S2.Pin_1, S2.Pin_2, S2.Pin_3, S2.Pin_4
  N1: Raspberry_Pi1.GPIO3, Raspberry_Pi1.GND, Raspberry_Pi1.GIPO21, Raspberry_Pi1.GIPO15, R26.Pin_1, LED2.cathode, LED4.cathode, LED5.cathode, LED6.cathode, LED7.cathode, R28.Pin_1, U3.D, U5.pin1
  N2: Raspberry_Pi1.GIPO4, R4.Pin_1
  N3: Raspberry_Pi1.GIPO17, R7.Pin_1
  N4: Raspberry_Pi1.GIPO27, R9.Pin_1
  N5: Raspberry_Pi1.GIPO22, R10.Pin_1
  N6: Raspberry_Pi1.GIPO10, U3.B
  N7: Raspberry_Pi1.GIPO9, U3.A
  N8: Raspberry_Pi1.GIPO11, U3.F
  N9: Raspberry_Pi1.GIPO5, R19.Pin_1
  N10: Raspberry_Pi1.GIPO6, U4.E
  N11: Raspberry_Pi1.GIPO13, U4.C
  N12: Raspberry_Pi1.GIPO19, U4.B
  N13: Raspberry_Pi1.GIPO26, U4.F
  N14: Raspberry_Pi1.GIPO20, U4.G
  N15: Raspberry_Pi1.GIPO16, U4.A
  N16: Raspberry_Pi1.GIPO12, U4.D
  N17: Raspberry_Pi1.GIPO8, U3.G
  N18: Raspberry_Pi1.GIPO25, R15.Pin_1
  N19: Raspberry_Pi1.GIPO23, R29.Pin_0
  N20: Raspberry_Pi1.GIPO18, U3.C
  N21: Raspberry_Pi1.GIPO14, U3.E
  N22: R7.Pin_0, LED2.anode
  N23: R9.Pin_0, LED3.anode
  N24: R10.Pin_0, LED4.anode
  N25: R12.Pin_0, LED5.anode
  N26: R15.Pin_0, LED6.anode
  N27: R19.Pin_0, LED7.anode
  N28: R28.Pin_0, U3.G2, U4.G2
  N29: R29.Pin_1, U5.pin2

custom parts:
  Raspberry Pi B+: The awesome Raspberry Pi ARM Board with 40 pin gipo. Ready for special designed Raspberry Pi B+ Hat (Hardware attached (on) top)
  Mystery Part - 2 pins: A dummy, proxy, ersatz, stand-in part for whatever you want. With 2 pins on a 100 mil inline pin header footprint.
